# Fritzing sketch ET2000_stupidlight (saved by Fritzing 0.9.10b)
breadboards: 1

parts:
  PIR1 = PIR sensor
  Part1 = BH1750
  Part2 = Arduino Uno (Rev3)
  R1 = Resistor [tolerance=±5% power=0.25 resistance=510 package=THT]
  R2 = Resistor [tolerance=±5% power=0.25 resistance=510 package=THT]
  R3 = Resistor [tolerance=±5% power=0.25 resistance=510 package=THT]
  U1 = RELAY [package=relay-g5q]
  LED1 = LED - 5mm [color="Red (633nm)" current=0.030 package="5 mm [THT]"]

nets:
  VDD: PIR1.VDD, Part1.VCC, Part2.3V3, U1.MAIN
  N1: PIR1.SIG, Part2.D4
  GND: PIR1.GND, Part1.GND, Part2.GND, U1.NC, U1.COIL1, LED1.cathode
  N2: Part1.SCL, R3.Pin_0
  N3: Part1.SDA, R2.Pin_0
  N4: Part1.ADDR, R1.Pin_0
  N5: Part2.A3, R1.Pin_1
  N6: Part2.A4/SDA, R2.Pin_1
  N7: Part2.A5/SCL, R3.Pin_1
  N8: Part2.D13/SCK, U1.NO
  N9: U1.COIL2, LED1.anode

custom parts:
  BH1750: Light Sensor
